# Fritzing sketch schematic (saved by Fritzing 0.9.4)
breadboards: 1

parts:
  Raspberry_Pi_2 = Raspberry Pi 3 [part_number=RPI-3-V1.2]
  S1 = Pushbutton [package="[THT]"]
  R1 = Resistor [tolerance=±5% resistance=10k package="0402 [SMD]"]

nets:
  N1: Raspberry_Pi_2.GPIO14, S1.Pin_1, S1.Pin_2, R1.Pin_1
  N2: Raspberry_Pi_2.GND, S1.Pin_3, S1.Pin_4, R1.Pin_0
